# Fritzing sketch FourTins (saved by Fritzing 0.9.3b)
breadboards: 1

parts:
  J1 = Basic Servo
  J2 = Basic Servo
  J3 = Basic Servo
  J4 = Basic Servo
  J5 = Piezo Speaker
  J6 = Piezo Speaker
  J7 = Piezo Speaker
  J8 = Piezo Speaker
  Part1 = Arduino Uno (Rev3)
  LED1 = LEDs [package=led10mm]
  R2 = Resistor [tolerance=±5% resistance=3.3M package=THT]
  VCC1 = Battery block 9V
  R5 = Resistor [tolerance=±5% resistance=3.3M package=THT]
  R6 = Resistor [tolerance=±5% resistance=3.3M package=THT]
  R7 = Resistor [tolerance=±5% resistance=3.3M package=THT]
  LED2 = LEDs [package=led10mm]
  LED3 = LEDs [package=led10mm]
  LED4 = LEDs [package=led10mm]

nets:
  GND: J1.gnd, J2.gnd, J3.gnd, J4.gnd, J5.pin1, J6.pin1, J7.pin1, J8.pin1, R2.Pin_1, R5.Pin_1, R6.Pin_1, R7.Pin_1
  VCC: J1.vcc, J2.vcc, J3.vcc, J4.vcc
  N1: J1.pulse, Part1.D3_PWM
  N2: J2.pulse, Part1.D5_PWM
  N3: J3.pulse, Part1.D6_PWM
  N4: J4.pulse, Part1.D9_PWM
  N5: J5.pin2, Part1.A0, R2.Pin_0
  N6: J6.pin2, Part1.A1, R5.Pin_0
  N7: J7.pin2, Part1.A2, R6.Pin_0
  N8: J8.pin2, Part1.A3, R7.Pin_0
  N9: Part1.D10_PWM/SS, LED1.A
  N10: Part1.D11_PWM/MOSI, LED2.A
  N11: Part1.D12/MISO, LED3.A
  N12: Part1.D13/SCK, LED4.A
  N13: Part1.GND, VCC1.-
  N14: Part1.VIN, VCC1.+
